// Logisim project GOAT 4BitALU.circ as structural Verilog: 17 circuits, main circuit 4-Bit ALU
module _4_Bit_ALU (
  input  A3,
  input  A2,
  input  A1,
  input  A0,
  input  B3,
  input  B2,
  input  B1,
  input  B0,
  input  S2,
  input  S1,
  input  S0,
  output OF,
  output R3,
  output R2,
  output R1,
  output R0
);

  wire [3:0] interface_1_r, undriven, undriven_2;

  Hex_Digit_Display hex_digit_display_1 (.value(undriven), .dp(1'b0));
  Hex_Digit_Display hex_digit_display_2 (.value(undriven_2), .dp(1'b0));
  Interface interface_1 (
    .A3(A3), .R3(R3), .A2(A2), .R2(R2), .A1(A1), .R1(R1), .A0(A0), .R0(R0), .B3(B3), .B2(B2), .B1(B1),
    .B0(B0), .S2(S2), .S1(S1), .S0(S0), .R(interface_1_r), .OF(OF));
  Hex_Digit_Display hex_digit_display_3 (.value(interface_1_r), .dp(1'b0));

  // Notes on the sheet:
  //   Kleinprojekt Arithmetic and Logic Unit
  //   Teamname:
  //   ausgeführt von
  //   kelvin.louis@students.fhnw.ch
  //   nicola.cocquio@students.fhnw.ch
  //   raphael.roussis@students.fhnw.ch
  //   vladimir.nikitovic@students.fhnw.ch
  //   GOAT
endmodule

module Interface (
  input  A0,
  input  A1,
  input  A2,
  input  A3,
  input  B0,
  input  B1,
  input  B2,
  input  B3,
  input  S0,
  input  S1,
  input  S2,
  output [3:0] R,
  output R0,
  output R1,
  output R2,
  output R3,
  output OF
);

  wire n4_bit_splitter_adder_1_overflow, n5_times_a_1_out_3;
  wire [2:0] n3_bit_splitter_1_out_4;
  wire [3:0] n4_bit_splitter_1_out_5, n4_bit_splitter_2_out_5, n4_bit_splitter_adder_1_r,
       n4_bit_splitter_and_1_out_3, n4_bit_splitter_not_1_out_2, n4_bit_splitter_not_2_out_2,
       n4_bit_splitter_or_1_out_3, n5_times_a_1_out_2;

  _4_Bit_Splitter u_4_bit_splitter_1 (.X0(A0), .X1(A1), .X2(A2), .X3(A3), .out_5(n4_bit_splitter_1_out_5));
  _4_Bit_Splitter u_4_bit_splitter_2 (.X0(B0), .X1(B1), .X2(B2), .X3(B3), .out_5(n4_bit_splitter_2_out_5));
  _3_Bit_Splitter u_3_bit_splitter_1 (.X0(S0), .X1(S1), .X2(S2), .out_4(n3_bit_splitter_1_out_4));
  _4_Bit_Splitter_OR u_4_bit_splitter_or_1 (
    .A(n4_bit_splitter_1_out_5), .B(n4_bit_splitter_2_out_5), .out_3(n4_bit_splitter_or_1_out_3));
  _4_Bit_Splitter_AND u_4_bit_splitter_and_1 (
    .A(n4_bit_splitter_1_out_5), .B(n4_bit_splitter_2_out_5), .out_3(n4_bit_splitter_and_1_out_3));
  _4_Bit_Splitter_NOT u_4_bit_splitter_not_1 (.A(n4_bit_splitter_1_out_5), .out_2(n4_bit_splitter_not_1_out_2));
  _4_Bit_Splitter_NOT u_4_bit_splitter_not_2 (.A(n4_bit_splitter_2_out_5), .out_2(n4_bit_splitter_not_2_out_2));
  _4_Bit_Splitter_Adder u_4_bit_splitter_adder_1 (
    .A(n4_bit_splitter_1_out_5), .B(n4_bit_splitter_2_out_5), .R(n4_bit_splitter_adder_1_r),
    .Overflow(n4_bit_splitter_adder_1_overflow));
  _5_times_A u_5_times_a_1 (.in_1(n4_bit_splitter_1_out_5), .out_2(n5_times_a_1_out_2), .out_3(n5_times_a_1_out_3));
  _8_1_MUX_Splitter u_8_1_mux_splitter_1 (
    .X0(n4_bit_splitter_or_1_out_3), .X1(n4_bit_splitter_and_1_out_3), .X2(n4_bit_splitter_not_1_out_2),
    .X3(n4_bit_splitter_not_2_out_2), .X4(n4_bit_splitter_adder_1_r), .X7(n5_times_a_1_out_2), .out_10(R),
    .R0(R0), .R1(R1), .R2(R2), .R3(R3), .S(n3_bit_splitter_1_out_4));  // open: X5, X6
endmodule

module blackbox (
);

  _4_Bit_ALU u_4_bit_alu_1 ();  // open: A3, A2, A1, A0, B3, B2, B1, B0, S2, S1, S0, OF, R3, R2, R1, R0
endmodule

module _4_Bit_Splitter_OR (
  input  [3:0] A,
  input  [3:0] B,
  output [3:0] out_3
);

  wire n4_bit_or_1_r0, n4_bit_or_1_r1, n4_bit_or_1_r2, n4_bit_or_1_r3;

  _4_Bit_OR u_4_bit_or_1 (
    .A0(A[0]), .B0(B[0]), .A1(A[1]), .B1(B[1]), .A2(A[2]), .B2(B[2]), .A3(A[3]), .B3(B[3]),
    .R0(n4_bit_or_1_r0), .R1(n4_bit_or_1_r1), .R2(n4_bit_or_1_r2), .R3(n4_bit_or_1_r3));
  _4_Bit_Splitter u_4_bit_splitter_1 (
    .X0(n4_bit_or_1_r0), .X1(n4_bit_or_1_r1), .X2(n4_bit_or_1_r2), .X3(n4_bit_or_1_r3), .out_5(out_3));

  // Notes on the sheet:
  //   4-Bit Splitter OR
endmodule

module _4_Bit_Splitter_AND (
  input  [3:0] A,
  input  [3:0] B,
  output [3:0] out_3
);

  wire n4_bit_and_1_r0, n4_bit_and_1_r1, n4_bit_and_1_r2, n4_bit_and_1_r3;

  _4_Bit_AND u_4_bit_and_1 (
    .A0(A[0]), .B0(B[0]), .A1(A[1]), .B1(B[1]), .A2(A[2]), .B2(B[2]), .A3(A[3]), .B3(B[3]),
    .R0(n4_bit_and_1_r0), .R1(n4_bit_and_1_r1), .R2(n4_bit_and_1_r2), .R3(n4_bit_and_1_r3));
  _4_Bit_Splitter u_4_bit_splitter_1 (
    .X0(n4_bit_and_1_r0), .X1(n4_bit_and_1_r1), .X2(n4_bit_and_1_r2), .X3(n4_bit_and_1_r3), .out_5(out_3));

  // Notes on the sheet:
  //   4-Bit Splitter AND
endmodule

module _4_Bit_Splitter_NOT (
  input  [3:0] A,
  output [3:0] out_2
);

  wire n4_bit_not_1_r0, n4_bit_not_1_r1, n4_bit_not_1_r2, n4_bit_not_1_r3;

  _4_Bit_NOT u_4_bit_not_1 (
    .X0(A[0]), .X1(A[1]), .X2(A[2]), .X3(A[3]), .R0(n4_bit_not_1_r0), .R1(n4_bit_not_1_r1),
    .R2(n4_bit_not_1_r2), .R3(n4_bit_not_1_r3));
  _4_Bit_Splitter u_4_bit_splitter_1 (
    .X0(n4_bit_not_1_r0), .X1(n4_bit_not_1_r1), .X2(n4_bit_not_1_r2), .X3(n4_bit_not_1_r3), .out_5(out_2));

  // Notes on the sheet:
  //   4-Bit Splitter NOT
endmodule

module _4_Bit_Splitter_Adder (
  input  [3:0] A,
  input  [3:0] B,
  output [3:0] R,
  output Overflow
);

  wire n4_bit_adder_1_r0, n4_bit_adder_1_r1, n4_bit_adder_1_r2, n4_bit_adder_1_r3;

  _4_Bit_Adder u_4_bit_adder_1 (
    .A0(A[0]), .B0(B[0]), .A1(A[1]), .B1(B[1]), .A2(A[2]), .B2(B[2]), .A3(A[3]), .B3(B[3]),
    .R0(n4_bit_adder_1_r0), .R1(n4_bit_adder_1_r1), .R2(n4_bit_adder_1_r2), .R3(n4_bit_adder_1_r3),
    .C(Overflow));
  _4_Bit_Splitter u_4_bit_splitter_1 (
    .X0(n4_bit_adder_1_r0), .X1(n4_bit_adder_1_r1), .X2(n4_bit_adder_1_r2), .X3(n4_bit_adder_1_r3), .out_5(R));

  // Notes on the sheet:
  //   4-Bit Splitter AND
endmodule

module _4_Bit_OR (
  input  A0,
  input  B0,
  input  A1,
  input  B1,
  input  A2,
  input  B2,
  input  A3,
  input  B3,
  output R0,
  output R1,
  output R2,
  output R3
);

  or or_1 (R0, A0, B0);
  or or_2 (R1, A1, B1);
  or or_3 (R2, A2, B2);
  or or_4 (R3, A3, B3);

  // Notes on the sheet:
  //   4-Bit OR
endmodule

module _4_Bit_AND (
  input  A0,
  input  B0,
  input  A1,
  input  B1,
  input  A2,
  input  B2,
  input  A3,
  input  B3,
  output R0,
  output R1,
  output R2,
  output R3
);

  and and_1 (R0, A0, B0);
  and and_2 (R1, A1, B1);
  and and_3 (R2, A2, B2);
  and and_4 (R3, A3, B3);

  // Notes on the sheet:
  //   4-Bit AND
endmodule

module _4_Bit_NOT (
  input  X0,
  input  X1,
  input  X2,
  input  X3,
  output R0,
  output R1,
  output R2,
  output R3
);

  not not_1 (R0, X0);
  not not_2 (R1, X1);
  not not_3 (R2, X2);
  not not_4 (R3, X3);

  // Notes on the sheet:
  //   4-Bit NOT
endmodule

module _4_Bit_Adder (
  input  A0,
  input  B0,
  input  A1,
  input  B1,
  input  A2,
  input  B2,
  input  A3,
  input  B3,
  output R0,
  output R1,
  output R2,
  output R3,
  output C
);

  wire va_1_co, va_2_co, va_3_co;

  VA va_1 (.x1(B0), .x0(A0), .ci(1'b0), .co(va_1_co), .s(R0));
  VA va_2 (.x1(B1), .x0(A1), .ci(va_1_co), .co(va_2_co), .s(R1));
  VA va_3 (.x1(B2), .x0(A2), .ci(va_2_co), .co(va_3_co), .s(R2));
  VA va_4 (.x1(B3), .x0(A3), .ci(va_3_co), .co(C), .s(R3));
endmodule

module VA (
  input  x1,
  input  x0,
  input  ci,
  output co,
  output s
);

  wire ha_1_c, ha_1_s, ha_2_c;

  HA ha_1 (.x1(x1), .x0(x0), .c(ha_1_c), .s(ha_1_s));
  HA ha_2 (.x1(ha_1_s), .x0(ci), .c(ha_2_c), .s(s));
  or or_1 (co, ha_1_c, ha_2_c);

  // Notes on the sheet:
  //   VA: Volladdierer
endmodule

module HA (
  input  x1,
  input  x0,
  output c,
  output s
);

  and and_1 (c, x1, x0);
  xor xor_1 (s, x1, x0);

  // Notes on the sheet:
  //   HA: Halbaddierer
endmodule

module _8_1_MUX_Splitter (
  input  [3:0] X0,
  input  [3:0] X1,
  input  [3:0] X2,
  input  [3:0] X3,
  input  [3:0] X4,
  input  [3:0] X5,
  input  [3:0] X6,
  input  [3:0] X7,
  input  [2:0] S,
  output [3:0] out_10,
  output R0,
  output R1,
  output R2,
  output R3
);

  Multiplexer #(.select(3), .width(4), .disabled(0), .enable("false")) multiplexer_1 (
    .in0(X0), .in1(X1), .in2(X2), .in3(X3), .in4(X4), .in5(X5), .in6(X6), .in7(X7), .out(out_10), .sel(S));

  assign R0 = out_10[0];
  assign R1 = out_10[1];
  assign R2 = out_10[2];
  assign R3 = out_10[3];

  // Notes on the sheet:
  //   8:1 MUX Splitter
endmodule

module _3_Bit_Splitter (
  input  X0,
  input  X1,
  input  X2,
  output [2:0] out_4
);


  assign out_4 = {X2, X1, X0};

  // Notes on the sheet:
  //   3-Bit Splitter
endmodule

module _4_Bit_Splitter (
  input  X0,
  input  X1,
  input  X2,
  input  X3,
  output [3:0] out_5
);


  assign out_5 = {X3, X2, X1, X0};

  // Notes on the sheet:
  //   4-Bit Splitter
endmodule

module _5_times_A (
  input  [3:0] in_1,
  output [3:0] out_2,
  output out_3
);

  wire n4_bit_adder_1_c, n4_bit_adder_1_r0, n4_bit_adder_1_r1, n4_bit_adder_1_r2, n4_bit_adder_1_r3,
       n4_bit_adder_2_c, n4_bit_adder_2_r0, n4_bit_adder_2_r1, n4_bit_adder_2_r2, n4_bit_adder_2_r3,
       n4_bit_adder_3_c, n4_bit_adder_3_r0, n4_bit_adder_3_r1, n4_bit_adder_3_r2, n4_bit_adder_3_r3,
       n4_bit_adder_4_c;

  _4_Bit_Adder u_4_bit_adder_1 (
    .A0(in_1[0]), .B0(in_1[0]), .A1(in_1[1]), .B1(in_1[1]), .A2(in_1[2]), .B2(in_1[2]), .A3(in_1[3]),
    .B3(in_1[3]), .R0(n4_bit_adder_1_r0), .R1(n4_bit_adder_1_r1), .R2(n4_bit_adder_1_r2),
    .R3(n4_bit_adder_1_r3), .C(n4_bit_adder_1_c));
  _4_Bit_Adder u_4_bit_adder_2 (
    .A0(in_1[0]), .B0(n4_bit_adder_1_r0), .A1(in_1[1]), .B1(n4_bit_adder_1_r1), .A2(in_1[2]),
    .B2(n4_bit_adder_1_r2), .A3(in_1[3]), .B3(n4_bit_adder_1_r3), .R0(n4_bit_adder_2_r0),
    .R1(n4_bit_adder_2_r1), .R2(n4_bit_adder_2_r2), .R3(n4_bit_adder_2_r3), .C(n4_bit_adder_2_c));
  _4_Bit_Adder u_4_bit_adder_3 (
    .A0(in_1[0]), .B0(n4_bit_adder_2_r0), .A1(in_1[1]), .B1(n4_bit_adder_2_r1), .A2(in_1[2]),
    .B2(n4_bit_adder_2_r2), .A3(in_1[3]), .B3(n4_bit_adder_2_r3), .R0(n4_bit_adder_3_r0),
    .R1(n4_bit_adder_3_r1), .R2(n4_bit_adder_3_r2), .R3(n4_bit_adder_3_r3), .C(n4_bit_adder_3_c));
  _4_Bit_Adder u_4_bit_adder_4 (
    .A0(in_1[0]), .B0(n4_bit_adder_3_r0), .A1(in_1[1]), .B1(n4_bit_adder_3_r1), .A2(in_1[2]),
    .B2(n4_bit_adder_3_r2), .A3(in_1[3]), .B3(n4_bit_adder_3_r3), .R0(out_2[0]), .R1(out_2[1]),
    .R2(out_2[2]), .R3(out_2[3]), .C(n4_bit_adder_4_c));
  or or_1 (out_3, n4_bit_adder_4_c, n4_bit_adder_3_c, n4_bit_adder_2_c, n4_bit_adder_1_c);
endmodule
